# Fritzing sketch mobile-main (saved by Fritzing 0.9.3b)
circuit board: 11cm x 5.51083cm
circuit board: 11cm x 14cm
breadboards: 1

parts:
  IC1 = DIP - 14 pins [chip_label=IC package="DIP (Dual Inline) [THT]"]
  R1 = Trimmer Potentiometer [maximum_resistance=10kΩ package=THT]
  R2 = Trimmer Potentiometer [maximum_resistance=10kΩ package=THT]
  R3 = Trimmer Potentiometer [maximum_resistance=10kΩ package=THT]
  R4 = Trimmer Potentiometer [maximum_resistance=10kΩ package=THT]
  R5 = Trimmer Potentiometer [maximum_resistance=10kΩ package=THT]
  R6 = Trimmer Potentiometer [maximum_resistance=10kΩ package=THT]
  LED1 = LED - 3mm [color="Red (633nm)" package="3 mm [THT]"]
  LED2 = LED - 3mm [color="Red (633nm)" package="3 mm [THT]"]
  LED3 = LED - 3mm [color="Red (633nm)" package="3 mm [THT]"]
  LED4 = LED - 3mm [color="Red (633nm)" package="3 mm [THT]"]
  LED5 = LED - 3mm [color="Red (633nm)" package="3 mm [THT]"]
  LED6 = LED - 3mm [color="Red (633nm)" package="3 mm [THT]"]
  R7 = Resistor [tolerance=±5% resistance=470 package=THT]
  R8 = Resistor [tolerance=±5% resistance=470 package=THT]
  R9 = Resistor [tolerance=±5% resistance=470 package=THT]
  R10 = Resistor [tolerance=±5% resistance=470 package=THT]
  R11 = Resistor [tolerance=±5% resistance=470 package=THT]
  R12 = Resistor [tolerance=±5% resistance=470 package=THT]
  Part1 = Arduino Mega 2560 (Rev3)
  J8 = Camdenboss CTB0158-2 [part_number=CTB0158-2 package=THT]
  J9 = Camdenboss CTB0158-2 [part_number=CTB0158-2 package=THT]
  L293D1 = L293D [package=THT]
  J10 = Voltage Reguator [form="♀ (female)" package=THT]
  J11 = Camdenboss CTB0158-2 [part_number=CTB0158-2 package=THT]
  S6 = SPST Switch [package=switch-spdt]
  S9 = SWITCH-MOMENTARY-2 [package=tactile-pth-12mm]
  LED7 = LED - 3mm [color="Red (633nm)" package="3 mm [THT]"]
  R13 = Resistor [tolerance=±5% resistance=470 package=THT]
  S10 = Momentary Switch [package=ksa_sealed_tac_switch]
  LCD1 = LCD screen
  R14 = Trimmer Potentiometer [maximum_resistance=10kΩ package=THT]
  R15 = Trimmer Potentiometer [maximum_resistance=10kΩ package=THT]
  R16 = Resistor [tolerance=±5% resistance=220 package=THT]
  J12 = female pin header, 2 pins [form="♀ (female)"]
  S11 = SWITCH-MOMENTARY-2 [package=tactile-pth-12mm]
  S8 = Momentary Switch [package=ksa_sealed_tac_switch]
  S12 = Momentary Switch [package=ksa_sealed_tac_switch]
  IC2 = DIP - 14 pins [chip_label=IC package="DIP (Dual Inline) [THT]"]

nets:
  N1: IC1.OUT1, LED2.anode, Part1.D25
  N2: IC1.IN1+, R2.wiper
  5V: IC1.V+, R5.leg2, R6.leg2, Part1.5V, L293D1.+V, J10.VO+, R13.Pin_1, LCD1.VDD, R14.leg1, IC2.V+
  N3: IC1.IN2+, R1.wiper
  N4: IC1.OUT2, LED1.anode, R9.Pin_1, Part1.D23
  N5: IC1.OUT3, Part1.D29
  GND: IC1.GND, R5.leg1, R6.leg1, LED1.cathode, LED6.cathode, R7.Pin_1, R8.Pin_1, R9.Pin_0, R10.Pin_0, R11.Pin_0, R12.Pin_0, IC2.GND
  N6: IC1.IN4+, R5.wiper
  N7: IC1.OUT4, LED3.anode, Part1.D27
  N8: R1.leg1, R2.leg1
  N9: R1.leg2, R2.leg2
  N10: R3.leg1, R4.leg1
  N11: R3.wiper, IC2.IN4+
  N12: R3.leg2, R4.leg2
  N13: R4.wiper, IC2.IN3+
  N14: R6.wiper, IC2.IN1+
  N15: LED2.cathode, R7.Pin_0
  N16: LED3.cathode, R8.Pin_0
  N17: LED4.cathode, R12.Pin_1
  N18: LED4.anode, Part1.D49, IC2.OUT1
  N19: LED5.cathode, R11.Pin_1
  N20: LED5.anode, Part1.D51, IC2.OUT4
  N21: LED6.anode, R10.Pin_1, Part1.D53, IC2.OUT3
  GND_2: Part1.GND, L293D1.0V, J10.GND, J11.pin1, S9.2, LED7.cathode, S10.1, S10.3, LCD1.LED-, S11.2, S8.2, S8.4, S12.1, S12.3
  N22: Part1.D12_PWM, L293D1.In_2
  N23: Part1.D10_PWM, L293D1.In_1
  N24: Part1.D9_PWM, L293D1.Enable_1
  N25: Part1.D8_PWM, L293D1.In_4
  N26: Part1.RESET, S9.1
  N27: Part1.D5_PWM, L293D1.In_3
  N28: Part1.D6_PWM, L293D1.Enable_2
  N29: Part1.D22, LCD1.R/W
  N30: Part1.D24, LCD1.E
  N31: Part1.D34, LCD1.DB4
  N32: Part1.D36, LCD1.DB5
  N33: Part1.D38, LCD1.DB6
  N34: Part1.D40, LCD1.DB7
  N35: Part1.D47, IC2.OUT2
  N36: J8.pin1, L293D1.Out_3_(_Controlled_by_Enable_2_)
  N37: J8.pin2, L293D1.Out_4_(_Controlled_by_Enable_2_)
  N38: J9.pin1, L293D1.Out_1_(_Controlled_by_Enable_1_)
  N39: J9.pin2, L293D1.Out_2_(_Controlled_by_Enable_1_)
  N40: L293D1.+Vmotor, J10.IN+, S6.P
  N41: J11.pin2, S6.O
  N42: LED7.anode, R13.Pin_0
  N43: S10.2, S10.4
  N44: LCD1.V0, R14.wiper
  N45: LCD1.LED+, R15.leg1
  N46: R15.wiper, J12.pin2
  N47: R16.Pin_0, J12.pin1
  N48: S8.1, S8.3
  N49: S12.2, S12.4

custom parts:
  DIP - 14 pins: A DIP stand-in part for whatever IC you want. With 14 pins on a 300mil dual inline package (DIP) footprint.
  Voltage Reguator: 12v-3v3 Adjustable regulator
